# Fritzing sketch Display7Segment (saved by Fritzing 1.0.4)
breadboards: 1

parts:
  A1 = Raspberry Pi 5
  R1 = Resistor [tolerance=±5% power=0.25W resistance=220 package=THT]
  R2 = Resistor [tolerance=±5% power=0.25W resistance=220 package=THT]
  R3 = Resistor [tolerance=±5% power=0.25W resistance=220 package=THT]
  R4 = Resistor [tolerance=±5% power=0.25W resistance=220 package=THT]
  R5 = Resistor [tolerance=±5% power=0.25W resistance=220 package=THT]
  R6 = Resistor [tolerance=±5% power=0.25W resistance=220 package=THT]
  R8 = Resistor [tolerance=±5% power=0.25W resistance=220 package=THT]
  R9 = Resistor [tolerance=±5% power=0.25W resistance=220 package=THT]
  DI1 = 7 Segment Display

nets:
  N1: A1.GND, DI1.common_cathode
  N2: A1.GPIO22, R8.Pin_0
  N3: A1.GPIO23, R1.Pin_0
  N4: A1.GPIO24, R2.Pin_0
  N5: A1.GPIO25, R3.Pin_0
  N6: A1.GPIO12, R4.Pin_0
  N7: A1.GPIO16, R5.Pin_0
  N8: A1.GPIO20, R6.Pin_0
  N9: A1.GPIO21, R9.Pin_0
  N10: R1.Pin_1, DI1.Segment_B
  N11: R2.Pin_1, DI1.Segment_C
  N12: R3.Pin_1, DI1.Segment_DP
  N13: R4.Pin_1, DI1.Segment_G
  N14: R5.Pin_1, DI1.Segment_F
  N15: R6.Pin_1, DI1.Segment_E
  N16: R8.Pin_1, DI1.Segment_A
  N17: R9.Pin_1, DI1.Segment_D

notes:
  7 SEGMENT DISPLAY
  driven by Raspberry PI 5 with python gpiozero library

custom parts:
  Raspberry Pi 5: The RPi5, a faster version of the awesome Raspberry Pi4B ARM Board with 40 pin gpio.
