# Fritzing sketch display_4digit (saved by Fritzing 1.0.4)
breadboards: 1

parts:
  A1 = Raspberry Pi 5
  IC1 = L293D [package=THT]
  7_Segment_4_Digit_Display1 = 7-SEGMENT-4DIGIT common cathode [part_number=HS420561K-32 package=7-segment-4digit-cathode]

nets (from the schematic view):
  N1: A1.3V3, IC1.Enable_1, IC1.Enable_2
  5V: A1.5V, A1.Fan-5V, IC1.+Vmotor, IC1.+V
  GND: A1.GND, A1.Fan-GND, IC1.0V
  N2: A1.GPIO14, IC1.In_4
  N3: A1.GPIO15, 7_Segment_4_Digit_Display1.pin_1
  N4: A1.GPIO18, IC1.In_1
  N5: A1.GPIO23, IC1.In_2
  N6: A1.GPIO24, 7_Segment_4_Digit_Display1.pin_2
  N7: A1.GPIO25, IC1.In_3
  N8: A1.GPIO8, 7_Segment_4_Digit_Display1.pin_3
  N9: A1.GPIO7, 7_Segment_4_Digit_Display1.pin_4
  N10: A1.GPIO12, 7_Segment_4_Digit_Display1.pin_5
  N11: A1.GPIO16, 7_Segment_4_Digit_Display1.pin_7
  N12: A1.GPIO20, 7_Segment_4_Digit_Display1.pin_10
  N13: A1.GPIO21, 7_Segment_4_Digit_Display1.pin_11
  N14: IC1.Out_1_(_Controlled_by_Enable_1_), 7_Segment_4_Digit_Display1.pin_12
  N15: IC1.Out_2_(_Controlled_by_Enable_1_), 7_Segment_4_Digit_Display1.pin_9
  N16: IC1.Out_3_(_Controlled_by_Enable_2_), 7_Segment_4_Digit_Display1.pin_8
  N17: IC1.Out_4_(_Controlled_by_Enable_2_), 7_Segment_4_Digit_Display1.pin_6

notes:
  #1-E
  #2-D
  #3-DP
  #4-C
  #5-G
  #6-DIG4
  #7-B
  #8-DIG3
  #9-DIG2
  #10-F
  #11-A
  #12-DIG1

custom parts:
  Raspberry Pi 5: The RPi5, a faster version of the awesome Raspberry Pi4B ARM Board with 40 pin gpio.
  7-SEGMENT-4DIGIT common cathode: A 7 Segment 4 Digit common cathode display, with decimal points
